# Fritzing sketch schematics (saved by Fritzing 0.9.6b)
breadboards: 1

parts:
  Part1 = RFID-RC522 [part_number=101218]
  WeMos_D1_Mini1 = WeMos D1 Mini
  KY-1 = Keyes Relay [package=THT]
  S1 = Pushbutton [package="[SMD]"]
  R1 = Resistor [tolerance=±5% resistance=220 package="0805 [SMD]"]

nets:
  N1: Part1.SDA, WeMos_D1_Mini1.D8
  N2: Part1.SCK, WeMos_D1_Mini1.D5
  N3: Part1.MOSI, WeMos_D1_Mini1.D7
  N4: Part1.GND, WeMos_D1_Mini1.D3, WeMos_D1_Mini1.G, KY-1.ground, S1.Pin_1, S1.Pin_2, R1.Pin_0
  N5: Part1.RST, WeMos_D1_Mini1.D0
  N6: Part1.3.3V, KY-1.power, R1.Pin_1
  N7: WeMos_D1_Mini1.D4, KY-1.signal
  N8: S1.Pin_3, S1.Pin_4

custom parts:
  Keyes Relay: The Keyes 5V relay module is suitable for SCM development, home appliance control. It uses a 5V~12V TIL control signal which can control DC / AC signal.
