# Fritzing sketch schematics (saved by Fritzing 0.9.6b)
breadboards: 1

parts:
  Part1 = RFID-RC522 [part_number=101218]
  WeMos_D1_Mini1 = WeMos D1 Mini

nets:
  N1: Part1.SDA, WeMos_D1_Mini1.D8
  N2: Part1.SCK, WeMos_D1_Mini1.D5
  N3: Part1.GND, WeMos_D1_Mini1.G
  N4: Part1.RST, WeMos_D1_Mini1.A0
